# Fritzing sketch Drive Buddy GPIO pinout (saved by Fritzing 1.0.1rc)

parts:
  A1 = Raspberry Pi 5
  A2 = BBAA100043
  IC1 = Rasberry Pi NIOR Camera [chip_label=IC package="DIP (Dual Inline) [THT]"]  # not connected
  U2 = LCD-16X2 [package=lcd-16x2]
  LCM1602_IIC1 = LCM1602 IIC [part_number="LCM1602 IIC" chip_label="LCM1602 IIC" package="DIP (Dual Inline) [THT]"]
  GY-NEO6MV1 = GY-NEO6MV2
  SP1 = SPEAKER [package=pcb_mount_speaker]  # not connected

nets:
  VCC: A1.5V, A1.Fan-5V, LCM1602_IIC1.VCC, GY-NEO6MV1.Vcc
  N1: A1.GPIO2, LCM1602_IIC1.SDA
  N2: A1.GPIO3, LCM1602_IIC1.SCL
  GND: A1.GND, A2.pin4, LCM1602_IIC1.GND, GY-NEO6MV1.GND
  N3: A1.GPIO14, GY-NEO6MV1.Tx
  N4: A1.GPIO15, GY-NEO6MV1.Rx
  N5: A1.GPIO12, A2.pin1
  N6: A1.GPIO19, A2.pin3
  N7: A1.GPIO20, A2.pin2
  VSS: U2.VSS, LCM1602_IIC1.VSS
  VDD: U2.VDD, LCM1602_IIC1.VDD
  N8: U2.VO, LCM1602_IIC1.V0
  N9: U2.RS, LCM1602_IIC1.RS
  N10: U2.R_W, LCM1602_IIC1.RW
  N11: U2.E, LCM1602_IIC1.E
  N12: U2.DB0, LCM1602_IIC1.D0
  N13: U2.DB1, LCM1602_IIC1.D1
  N14: U2.DB2, LCM1602_IIC1.D2
  N15: U2.DB3, LCM1602_IIC1.D3
  N16: U2.DB4, LCM1602_IIC1.D4
  N17: U2.DB5, LCM1602_IIC1.D5
  N18: U2.DB6, LCM1602_IIC1.D6
  N19: U2.DB7, LCM1602_IIC1.D7
  N20: U2.A, LCM1602_IIC1.A
  N21: U2.K, LCM1602_IIC1.K
  N22: LCM1602_IIC1.LED_A, LCM1602_IIC1.LED_B

custom parts:
  Raspberry Pi 5: The RPi5, a faster version of the awesome Raspberry Pi4B ARM Board with 40 pin gpio.
  BBAA100043: BBAA100043 traffic light module.
  Rasberry Pi NIOR Camera: Camera
  LCM1602 IIC: I2C-Module to use a 1602 or 2004 LCD on with the wire.h libory Serial LCD Modul
  GY-NEO6MV2: Description: Module GPS , type GY-NEO6MV2, pour arduino et autres micro-contrôleurs. Caractéristiques De type GY-NEO6MV2 Alimentation 3V-5V Avec Flight Control EEPROM MWC Antenne large céramique, fort signal, 25 x 25 mm Paramètres de configuration sauvegardés en EEPROM Avec batterie de backup de données LED témoin de signal Module miniaturisé 25 x 35 mm Trou de fixation de 3mm Baud rate par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
